# Fritzing sketch DroneV7 (saved by Fritzing 0.9.5d)
circuit board: 8.46667cm x 5.64444cm
breadboards: 1

parts:
  IMU1 = IC, SIP package, 8 pins [chip_label=IMU]
  S1 = SO08 [chip_label=ESC package=SO]
  V1 = DC Power [voltage=12V]
  S2 = SO08 [chip_label=ESC package=SO]
  S3 = SO08 [chip_label=ESC package=SO]
  S4 = SO08 [chip_label=ESC package=SO]
  DC1 = IC, DIP package, 4 pins [chip_label=DC-DC]
  RES1 = IC, DIP package, 6 pins [chip_label=FS-iA6B]
  M1 = IC, SIP package, 4 pins [chip_label=BLDC]
  M2 = IC, SIP package, 4 pins [chip_label=BLDC]
  M3 = IC, SIP package, 4 pins [chip_label=BLDC]
  M4 = IC, SIP package, 4 pins [chip_label=BLDC]
  ESP1 = IC, DIP package, 42 pins [chip_label=ESP32-S3]
  CAM1 = IC, DIP package, 4 pins [chip_label="OV2640 Camera"]

nets:
  3.3V: IMU1.pin1, ESP1.pin1
  GND: IMU1.pin2, S1.3, S1.4, V1.V-, S2.3, S2.4, S3.3, S3.4, S4.3, S4.4, DC1.pin2, DC1.pin3, RES1.pin5, ESP1.pin23
  N1: IMU1.pin3, ESP1.pin24
  N2: IMU1.pin4, ESP1.pin25
  5V: S1.1, S2.1, S3.1, S4.1, DC1.pin4, RES1.pin6, ESP1.pin20
  N3: S1.2, ESP1.pin40
  N4: S1.5, M1.pin3
  N5: S1.6, M1.pin2
  N6: S1.7, M1.pin1
  12V: S1.8, V1.V+, S2.8, S3.8, S4.8, DC1.pin1
  N7: S2.2, ESP1.pin39
  N8: S2.5, M2.pin3
  N9: S2.6, M2.pin2
  N10: S2.7, M2.pin1
  N11: S3.2, ESP1.pin38
  N12: S3.5, M3.pin3
  N13: S3.6, M3.pin2
  N14: S3.7, M3.pin1
  N15: S4.2, ESP1.pin37
  N16: S4.5, M4.pin3
  N17: S4.6, M4.pin2
  N18: S4.7, M4.pin1
  N19: RES1.pin4, ESP1.pin41
  24x Camera Bus: ESP1.pin21, CAM1.pin4

notes:
  Droneanator 9000, G
